// Logisim project 8_bit_cpu.circ as structural Verilog
module FullAdder (
  input  in_1,
  input  in_2,
  input  in_3,
  output out_4,
  output out_5
);

  wire and_1_out, and_2_out, and_3_out;

  and and_1 (and_1_out, in_1, in_2);
  and and_2 (and_2_out, in_2, in_3);
  and and_3 (and_3_out, in_1, in_3);
  xor xor_1 (out_5, in_1, in_2, in_3);
  or or_1 (out_4, and_1_out, and_2_out, and_3_out);
endmodule

module Flipper (
  input  in_1,
  input  in_2,
  input  in_3,
  input  in_4,
  input  in_5,
  output out_6,
  output out_7,
  output out_8,
  output out_9
);

  xor xor_1 (out_6, in_1, in_5);
  xor xor_2 (out_7, in_2, in_5);
  xor xor_3 (out_8, in_3, in_5);
  xor xor_4 (out_9, in_4, in_5);
endmodule

module EightBitAdder (
  input  [7:0] in_1,
  input  [7:0] in_2,
  input  in_3,
  output out_4,
  output [7:0] out_5
);

  wire fourbitadder_2_out_4;

  FourBitAdder fourbitadder_1 (
    .in_1(in_1[7:4]), .in_2(in_2[7:4]), .in_3(fourbitadder_2_out_4), .out_4(out_4), .out_5(out_5[7:4]));
  FourBitAdder fourbitadder_2 (
    .in_1(in_1[3:0]), .in_2(in_2[3:0]), .in_3(in_3), .out_4(fourbitadder_2_out_4), .out_5(out_5[3:0]));
endmodule

module FourBitAdder (
  input  [3:0] in_1,
  input  [3:0] in_2,
  input  in_3,
  output out_4,
  output [3:0] out_5
);

  wire fulladder_2_out_4, fulladder_3_out_4, fulladder_4_out_4;

  FullAdder fulladder_1 (.in_1(in_1[3]), .in_2(in_2[3]), .in_3(fulladder_2_out_4), .out_5(out_5[3]), .out_4(out_4));
  FullAdder fulladder_2 (
    .in_1(in_1[2]), .in_2(in_2[2]), .in_3(fulladder_3_out_4), .out_5(out_5[2]), .out_4(fulladder_2_out_4));
  FullAdder fulladder_3 (
    .in_1(in_1[1]), .in_2(in_2[1]), .in_3(fulladder_4_out_4), .out_5(out_5[1]), .out_4(fulladder_3_out_4));
  FullAdder fulladder_4 (.in_1(in_1[0]), .in_2(in_2[0]), .in_3(in_3), .out_5(out_5[0]), .out_4(fulladder_4_out_4));
endmodule

module InbuiltAdder (
  input  [7:0] in_1,
  input  [7:0] in_2,
  input  in_3,
  output [7:0] out_4,
  output out_5
);

  wire [7:0] bit_extender_1_out, xor_1_out;

  assign bit_extender_1_out = {{7{in_3}}, in_3};  // Bit_Extender bit_extender_1
  assign xor_1_out = in_2 ^ bit_extender_1_out;  // XOR_Gate xor_1, 8 bits wide
  Adder adder_1 (.a(in_1), .b(xor_1_out), .out(out_4), .cin(in_3), .cout(out_5));
endmodule
